# Fritzing sketch stackduino-2-smd (saved by Fritzing 0.8.3b)
breadboards: 4

parts:
  Power_plug2 = Power plug
  Btn_3 = Pushbutton 12mm omron
  Encoder1 = Rotary Encoder with Knob
  Btn_4 = Pushbutton [package="[THT]"]
  Btn_5 = Pushbutton [package="[THT]"]
  C7 = Ceramic Capacitor [capacitance=0.1µF package="0805 [SMD, multilayer]"]  # not connected
  X1 = USB Connectors [package=usb-microb]
  C8 = Ceramic Capacitor [capacitance=100nF package="0805 [SMD, multilayer]"]  # not connected
  C9 = Ceramic Capacitor [capacitance=100nF package="0805 [SMD, multilayer]"]  # not connected
  C10 = Ceramic Capacitor [capacitance=100nF package="0805 [SMD, multilayer]"]
  C11 = Ceramic Capacitor [capacitance=100nF package="0805 [SMD, multilayer]"]
  R2 = Resistor [tolerance=±5% resistance=220 package="1206 [SMD]"]  # not connected
  U2 = ATmega328 [package=tqfp]
  R3 = Resistor [tolerance=±5% resistance=220 package="1206 [SMD]"]  # not connected
  R1 = Resistor [tolerance=±5% resistance=220 package="1206 [SMD]"]  # not connected
  XTAL1 = Crystal [frequency="16 Mhz" package=SMD]
  IC1 = USB to UART Bridge - FT232RL [chip_label=IC package=SSOP28DB]  # not connected
  L1 = Inductors [package=cdrh2d09]
  J2 = female pin header, 6 pins [form="♀ (female)"]  # not connected
  LTC1 = LTC4412 [package=ThinSOT]
  IC2 = ILD213T [package=so08]  # not connected
  MC34063A1 = MC34063A [package=so08]
  DB1 = DB15_rt_female  # not connected
  IC4 = SSOP24 [chip_label=IC package=SSOP]  # not connected
  A1 = Allegro A3967 [part_number=" A3967" chip_label=" A3967" package=SOIC-24]  # not connected
  J1 = Dig-ole 128 x 64 0.96" OLED Display [form="♀ (female)" package=THT]  # not connected
  Power_plug3 = Power plug
  R4 = Resistor [tolerance=±5% resistance=220 package=THT]
  C12 = Electrolytic Capacitor [capacitance=1µF package="100 mil [THT, electrolytic]"]
  C13 = Electrolytic Capacitor [capacitance=1µF package="100 mil [THT, electrolytic]"]
  R5 = Resistor [tolerance=±5% resistance=220 package=THT]
  D1 = Rectifier Diode [part_number=1N4001 package="300 mil [THT]"]
  C14 = Ceramic Capacitor [capacitance=100nF package="100 mil [THT, multilayer]"]
  D2 = Rectifier Diode [part_number=1N4001 package="300 mil [THT]"]
  Q1 = PNP-Transistor [package="TO92 [THT]"]
  R6 = Resistor [tolerance=±5% resistance=220 package=THT]
  C15 = Ceramic Capacitor [capacitance=100nF package="100 mil [THT, multilayer]"]
  C16 = Ceramic Capacitor [capacitance=100nF package="100 mil [THT, multilayer]"]

nets:
  N1: Power_plug2.VCC, D2.anode
  GND: Btn_3.Pin_4, Encoder1.no_name_yet#2, Encoder1.no_name_yet#5, Btn_4.Pin_3, Btn_4.Pin_4, Btn_5.Pin_3, Btn_5.Pin_4, X1.GND, C10.1, C11.0, U2.GND, U2.AGND, LTC1.2, LTC1.3, MC34063A1.4, C12.-, C13.-, R5.Pin_1, D1.cathode, C14.0, C15.0, C16.0
  N2: Btn_4.Pin_1, Btn_4.Pin_2
  N3: Btn_5.Pin_1, Btn_5.Pin_2
  N4: X1.VBUS, U2.VCC, U2.AVCC, U2.AREF, L1.2, MC34063A1.5, C13.+, R5.Pin_0, R6.Pin_1, C15.1, C16.1
  N5: C10.0, U2.PB7(XTAL2_TOSC2), XTAL1.pin_1
  N6: C11.1, U2.PB6(XTAL1_TOSC1), XTAL1.pin_0
  N7: L1.1, MC34063A1.2, D1.anode
  N8: LTC1.1, Power_plug3.VCC, Q1.E
  N9: LTC1.4, R6.Pin_0
  N10: LTC1.5, Q1.B
  N11: LTC1.6, MC34063A1.6, R4.Pin_1, C12.+, D2.cathode
  N12: MC34063A1.1, MC34063A1.7, MC34063A1.8, R4.Pin_0
  N13: MC34063A1.3, C14.1

notes:
  ATMEGA
  Regulated 5v
  Unregulated Vin
  DC Adapter
  Battery
  POWER
  A3967
  FT232RL

custom parts:
  Pushbutton 12mm omron: A generic pushbutton. 12mm
  Rotary Encoder with Knob: Rotary Encoder with 1/4" Shaft and Knob
  LTC4412: Low Loss Powerpath Controller
  MC34063A: 1.5 A, Step-Up/Down/Inverting Switching Regulator
  DB15_rt_female: 15 pin, right-angle female VGA connector. Based on DB9 part by Don Roberts.
  Allegro A3967: Allegro A3967 stepper motor driver in SOIC 24 package
